# Fritzing sketch ETHERNETARAYUZLU (saved by Fritzing 0.9.2b)

parts:
  Eleman1 = Arduino Uno (Rev3)  # not connected
  Eleman2 = Arduino Ethernet Shield (Rev3)
  T1 = LM35 Temperature Sensor [package="TO92 [THT]"]
  LED1 = LEDs [package=led10mm]
  J1 = Basic Servo

nets:
  N1: Eleman2.PWM_D9, J1.pulse
  N2: Eleman2.A3, T1.+Vs
  N3: Eleman2.A4/SDA, T1.Vout
  N4: Eleman2.A5/SCL, T1.GND
  N5: Eleman2.D2, LED1.C
  N6: Eleman2.PWM_D3, LED1.A
  5V: Eleman2.5V, J1.vcc
  GND: Eleman2.GND, J1.gnd

notes:
  PIR
