# Fritzing sketch EthernetDHTLDR (saved by Fritzing 0.9.2b)
breadboards: 1

parts:
  Eleman1 = Arduino Uno (Rev3)  # not connected
  Eleman2 = Arduino Ethernet Shield (Rev3)
  RHT1 = Humidity and Temperature Sensor RHT03
  R1 = Photocell (LDR) [package=THT]
  R2 = Resistor [tolerance=±5% resistance=4.7k package=THT]
  R3 = Resistor [tolerance=±5% resistance=10k package=THT]

nets:
  N1: Eleman2.A0, R1.pin_0, R3.Pin_1
  5V: Eleman2.5V, RHT1.Vcc, R1.pin_1, R2.Pin_0
  N2: Eleman2.GND, RHT1.GND_2, R3.Pin_0
  N3: RHT1.Data-signal, R2.Pin_1
