# Fritzing sketch ParticleGazAlarm (saved by Fritzing 0.9.2b)
breadboards: 1

parts:
  Eleman1 = Photon
  U1 = GAS_SENSOR [package=mq-3]
  J1 = Piezo Speaker

nets:
  N1: Eleman1.A0, U1.B1
  N2: Eleman1.GND, U1.H2, J1.pin1
  N3: Eleman1.VIN, U1.A1
  N4: Eleman1.D0, J1.pin2
