# Fritzing sketch PhotonWifiDedektor (saved by Fritzing 0.9.2b)
breadboards: 1

parts:
  Eleman1 = Photon
  D1 = LED_BARGRAPH_10 [package=led_bargaph_10]
  R1 = Resistor [tolerance=±5% resistance=220 package=THT]
  R2 = Resistor [tolerance=±5% resistance=220 package=THT]
  R3 = Resistor [tolerance=±5% resistance=220 package=THT]
  R4 = Resistor [tolerance=±5% resistance=220 package=THT]
  R5 = Resistor [tolerance=±5% resistance=220 package=THT]
  R6 = Resistor [tolerance=±5% resistance=220 package=THT]
  R7 = Resistor [tolerance=±5% resistance=220 package=THT]
  R8 = Resistor [tolerance=±5% resistance=220 package=THT]
  R9 = Resistor [tolerance=±5% resistance=220 package=THT]
  R10 = Resistor [tolerance=±5% resistance=220 package=THT]
  SPKR1 = Loudspeaker

nets:
  N1: Eleman1.A0, D1.I_C
  N2: Eleman1.A1, D1.J_C
  N3: Eleman1.RX, SPKR1.pin2
  N4: Eleman1.GND, R1.Pin_1, R2.Pin_1, R3.Pin_1, R4.Pin_1, R5.Pin_1, R6.Pin_1, R7.Pin_1, R8.Pin_1, R9.Pin_1, R10.Pin_1, SPKR1.pin1
  N5: Eleman1.D0, D1.A_C
  N6: Eleman1.D1, D1.B_C
  N7: Eleman1.D2, D1.C_C
  N8: Eleman1.D3, D1.D_C
  N9: Eleman1.D4, D1.E_C
  N10: Eleman1.D5, D1.F_C
  N11: Eleman1.D6, D1.G_C
  N12: Eleman1.D7, D1.H_C
  N13: D1.A_A, R9.Pin_0
  N14: D1.B_A, R8.Pin_0
  N15: D1.C_A, R6.Pin_0
  N16: D1.D_A, R7.Pin_0
  N17: D1.E_A, R10.Pin_0
  N18: D1.F_A, R5.Pin_0
  N19: D1.G_A, R4.Pin_0
  N20: D1.H_A, R3.Pin_0
  N21: D1.I_A, R2.Pin_0
  N22: D1.J_A, R1.Pin_0
