# Fritzing sketch RaspberrySıcaklıkNEM (saved by Fritzing 0.9.2b)
breadboards: 1

parts:
  Raspberry_Pi1 = Raspberry Pi 2
  RHT1 = Humidity and Temperature Sensor RHT03
  Grove1 = Grove OLED 128x96

nets:
  3V3: Raspberry_Pi1.3v3, Grove1.VCC
  N1: Raspberry_Pi1.GPIO2, Grove1.SDA
  N2: Raspberry_Pi1.GPIO3, Grove1.SCL
  N3: Raspberry_Pi1.GPIO4, RHT1.Data-signal
  GND: Raspberry_Pi1.GND, RHT1.GND_2, Grove1.GND
  5V: Raspberry_Pi1.5V, RHT1.Vcc
