# Fritzing sketch Untitled Sketch (saved by Fritzing 0.9.2b)
breadboards: 1

parts:
  Espessif_Serial_Wifi_Modul_1 = ESP8266 ESP01 [part_number=ESP8266 package=THT]
  R1 = Resistor [tolerance=±5% resistance=1k package="0402 [SMD]"]
  R2 = Resistor [tolerance=±5% resistance=2.2k package="0402 [SMD]"]
  Eleman1 = Arduino Uno (Rev3) - ICSP
  T1 = LM35 Temperature Sensor [package="TO92 [THT]"]

nets:
  N1: Espessif_Serial_Wifi_Modul_1.RXD, R1.Pin_1, R2.Pin_0
  N2: Espessif_Serial_Wifi_Modul_1.TXD, Eleman1.D10_PWM/SS
  VCC: Espessif_Serial_Wifi_Modul_1.VCC, Espessif_Serial_Wifi_Modul_1.CH_PD, Eleman1.3V3
  N3: R1.Pin_0, Eleman1.D11_PWM/MOSI
  GND: R2.Pin_1, Eleman1.GND, T1.GND
  N4: Eleman1.A0, T1.Vout
  N5: Eleman1.5V, T1.+Vs

custom parts:
  ESP8266 ESP01: Generic WiFi Module based on the ESP8266 with onboard PCB antenna and UART communications
