# Fritzing sketch yun (saved by Fritzing 0.9.2b)

parts:
  Eleman1 = SRF05 Ultrasonic Rangefinder
  Eleman2 = Arduino Yun

nets:
  VCC: Eleman1.VCC, Eleman2.5V
  N1: Eleman1.Trig, Eleman2.D2/SDA, Eleman2.D2
  N2: Eleman1.Echo, Eleman2.D4
  GND: Eleman1.GND, Eleman2.GND
